// Logisim project Lab_4.circ as structural Verilog: 5 circuits, main circuit main
module main (
  input  A3,
  input  A0,
  input  B0,
  input  B3,
  input  C0,
  input  A2,
  input  A1,
  input  B2,
  input  B1,
  output S3,
  output S0,
  output C4,
  output S2,
  output S1
);

  wire fulladder_1_cout, fulladder_2_cout, fulladder_4_cout;

  FullAdder fulladder_1 (.A(A0), .B(B0), .Cin(C0), .S(S0), .Cout(fulladder_1_cout));
  FullAdder fulladder_2 (.A(A1), .B(B1), .Cin(fulladder_1_cout), .S(S1), .Cout(fulladder_2_cout));
  FullAdder fulladder_3 (.A(A3), .B(B3), .Cin(fulladder_4_cout), .S(S3), .Cout(C4));
  FullAdder fulladder_4 (.A(A2), .B(B2), .Cin(fulladder_2_cout), .S(S2), .Cout(fulladder_4_cout));
endmodule

module FullAdder (
  input  A,
  input  B,
  input  Cin,
  output S,
  output Cout
);

  wire and_1_out, and_2_out, xor_1_out;

  xor xor_1 (xor_1_out, A, B);
  and and_1 (and_1_out, B, A);
  and and_2 (and_2_out, xor_1_out, Cin);
  xor xor_2 (S, xor_1_out, Cin);
  or or_1 (Cout, and_1_out, and_2_out);
endmodule

module HalfAdder (
  input  in_1,
  input  in_2,
  output out_3,
  output out_4
);

  xor xor_1 (out_3, in_1, in_2);
  and and_1 (out_4, in_1, in_2);
endmodule

module NAND_OR (
  input  A,
  input  B,
  output F_NAND,
  output F_OR
);

  wire nand_1_out, nand_2_out;

  or or_1 (F_OR, A, B);
  nand nand_1 (nand_1_out, A, A);
  nand nand_2 (nand_2_out, B, B);
  nand nand_3 (F_NAND, nand_1_out, nand_2_out);
endmodule

module OperationBlock (
  input  A,
  input  B,
  input  OP1,
  input  OP0,
  output F
);

  wire and_1_out, halfadder_1_out_3, or_1_out, xor_1_out;

  and and_1 (and_1_out, A, B);
  or or_1 (or_1_out, A, B);
  xor xor_1 (xor_1_out, A, B);
  HalfAdder halfadder_1 (.in_1(A), .in_2(B), .out_3(halfadder_1_out_3));  // open: out_4
  Multiplexer #(.select(2)) multiplexer_1 (
    .in0(and_1_out), .in1(or_1_out), .in2(xor_1_out), .in3(halfadder_1_out_3), .out(F), .sel({OP1, OP0}));
endmodule
